# Fritzing sketch TFT1.44esp32_withDHT22 (saved by Fritzing 0.9.3b)
circuit board: 15.3105cm x 9.92329cm
breadboards: 1

parts:
  DHT1 = DHT22 Humidity and Temperature Sensor
  TFT1_44_ST3375 = 1.44 inch TFT SPI
  U1 = ESP32S-HiLetgo [part_number=ESP32S-HiLetgo]

nets:
  N1: DHT1.VDD, U1.3.3
  N2: DHT1.DATA, U1.GPIO17
  GND: DHT1.GND, TFT1_44_ST3375.GND#9, U1.GND
  N3: TFT1_44_ST3375.CS, U1.GPIO6
  N4: TFT1_44_ST3375.RST, U1.GPIO4
  N5: TFT1_44_ST3375.RS, U1.GPIO2
  N6: TFT1_44_ST3375.SDI, U1.GPIO23
  N7: TFT1_44_ST3375.CLK, U1.GPIO18
  N8: TFT1_44_ST3375.LED, U1.VIN

notes:
  It's supposed to be a DHT22 module

custom parts:
  1.44 inch TFT SPI: 1.44 / TFT / SPI / ST3375
  ESP32S-HiLetgo: HiLetgo ESP-WROOM-32 ESP32 ESP-32S Development Board 2.4GHz Dual-Mode WiFi + Bluetooth Dual Cores Microcontroller The ESP32 integrated with Antenna switches, RF Balun, power amplifiers, low-noise amplifiers, filters, and management modules, and the entire solution occupies the least area of PCB. 2.4 GHz Wi-Fi plus Bluetooth dual-mode chip, with TSMC Ultra-low power consumption 40nm technology,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
